# Fritzing sketch schematics001 (saved by Fritzing 0.9.3b)
circuit board: 8.46667cm x 5.64444cm
breadboards: 1

parts:
  Raspberry_Pi_1 = Raspberry Pi 3 [part_number=RPI-3-V1.2]
  LED1 = LED - 5mm [color="White (6500K)" package="5 mm [THT]"]
  LED2 = LED - 5mm [color="Yellow (595nm)" package="5 mm [THT]"]
  LED3 = LED - 5mm [color="Red (633nm)" package="5 mm [THT]"]
  LED4 = LED - 5mm [color="Green (565nm)" package="5 mm [THT]"]
  LED5 = LED - 5mm [color="Blue (470nm)" package="5 mm [THT]"]
  LED6 = LED - 5mm [color="Green (555nm)" package="5 mm [THT]"]
  LED7 = LED - 5mm [color="Red (633nm)" package="5 mm [THT]"]
  R1 = Resistor [tolerance=±5% resistance=670 package=THT]

nets:
  N1: Raspberry_Pi_1.GPIO2, LED1.anode
  N2: Raspberry_Pi_1.GPIO3, LED2.anode
  N3: Raspberry_Pi_1.GPIO21, LED3.anode
  N4: Raspberry_Pi_1.GPIO20, LED4.anode
  N5: Raspberry_Pi_1.GPIO7, LED6.anode
  N6: Raspberry_Pi_1.GND, LED7.cathode, R1.Pin_1
  N7: Raspberry_Pi_1.GPIO23, LED5.anode
  N8: LED1.cathode, LED2.cathode, LED3.cathode, LED4.cathode, LED5.cathode, LED6.cathode, R1.Pin_0
